// Digital circuit 2demux.dig as structural Verilog
module _2demux (
  input  I,
  input  Sel,
  output O0,
  output O1
);

  wire nand_1_out, nand_2_out, not_1_out;

  nand nand_1 (nand_1_out, not_1_out, I);
  not not_1 (not_1_out, Sel);
  nand nand_2 (nand_2_out, Sel, I);
  not not_2 (O0, nand_1_out);
  not not_3 (O1, nand_2_out);
endmodule
