// Digital circuit 4demux.dig as structural Verilog
module _4demux (
  input  I,
  input  [1:0] Sel,
  output O0,
  output O1,
  output O2,
  output O3
);

  wire _1demux_1_p3, _1demux_1_p4;

  // _1demux _1demux_1: pin names not known; wires that end beside it: I, Sel[1], _1demux_1_p3, _1demux_1_p4
  // _1demux _1demux_2: pin names not known; wires that end beside it: _1demux_1_p3, Sel[0], O0, O1
  // _1demux _1demux_3: pin names not known; wires that end beside it: _1demux_1_p4, Sel[0], O2, O3
endmodule
