// Digital circuit 1mux.dig as structural Verilog
module _1mux (
  input  A,
  input  B,
  input  Sel,
  output O
);

  wire nand_1_out, nand_2_out, not_1_out;

  not not_1 (not_1_out, Sel);
  nand nand_1 (nand_1_out, A, not_1_out);
  nand nand_2 (nand_2_out, Sel, B);
  nand nand_3 (O, nand_1_out, nand_2_out);
endmodule
