// Digital circuit 2bitDecoder.dig as structural Verilog
module _2bitDecoder (
  input  [1:0] A,
  output _0,
  output _1,
  output _2,
  output _3
);

  wire not_1_out, not_2_out;

  not not_1 (not_1_out, A[1]);
  not not_2 (not_2_out, A[0]);
  nor nor_1 (_0, A[0], A[1]);
  nor nor_2 (_1, not_2_out, A[1]);
  nor nor_3 (_2, A[0], not_1_out);
  nor nor_4 (_3, not_2_out, not_1_out);
endmodule
