// Digital circuit 1mux.dig as structural Verilog
module _1mux (
  input  [1:0] Sel,
  input  A,
  input  B,
  input  C,
  input  D,
  output O
);

  wire _1mux_1_o, _1mux_2_o;

  _1mux _1mux_1 (.A(A), .B(B), .Sel(Sel[0]), .O(_1mux_1_o));
  _1mux _1mux_2 (.A(C), .B(D), .Sel(Sel[0]), .O(_1mux_2_o));
  _1mux _1mux_3 (.A(_1mux_1_o), .B(_1mux_2_o), .Sel(Sel[1]), .O(O));
endmodule
