// Digital circuit 2demux.dig as structural Verilog
module _2demux (
  input  [3:0] I,
  input  Sel,
  output [3:0] O0,
  output [3:0] O1
);

  _2demux _2demux_1 (.I(I[0]), .Sel(Sel), .O0(O0[0]), .O1(O1[0]));
  _2demux _2demux_2 (.I(I[1]), .Sel(Sel), .O0(O0[1]), .O1(O1[1]));
  _2demux _2demux_3 (.I(I[2]), .Sel(Sel), .O0(O0[2]), .O1(O1[2]));
  _2demux _2demux_4 (.I(I[3]), .Sel(Sel), .O0(O0[3]), .O1(O1[3]));
endmodule
