// Digital circuit 4demux.dig as structural Verilog
module _4demux (
  input  [3:0] I,
  input  [1:0] Sel,
  output [3:0] O0,
  output [3:0] O1,
  output [3:0] O2,
  output [3:0] O3
);

  // _1demux _1demux_1: pin names not known; wires that end beside it: I[0], Sel, O0[0], O1[0], O2[0], O3[0]
  // _1demux _1demux_2: pin names not known; wires that end beside it: I[1], Sel, O0[1], O1[1], O2[1], O3[1]
  // _1demux _1demux_3: pin names not known; wires that end beside it: I[2], Sel, O0[2], O1[2], O2[2], O3[2]
  // _1demux _1demux_4: pin names not known; wires that end beside it: I[3], Sel, O0[3], O1[3], O2[3], O3[3]
endmodule
