// Digital circuit 1mux.dig as structural Verilog
module _1mux (
  input  [3:0] A,
  input  [3:0] B,
  input  Sel,
  output [3:0] O
);

  _1mux _1mux_1 (.A(A[0]), .B(B[0]), .Sel(Sel), .O(O[0]));
  _1mux _1mux_2 (.A(A[1]), .B(B[1]), .Sel(Sel), .O(O[1]));
  _1mux _1mux_3 (.A(A[2]), .B(B[2]), .Sel(Sel), .O(O[2]));
  _1mux _1mux_4 (.A(A[3]), .B(B[3]), .Sel(Sel), .O(O[3]));
endmodule
