// Digital circuit 1mux.dig as structural Verilog
module _1mux (
  input  [3:0] A,
  input  [3:0] B,
  input  [3:0] C,
  input  [3:0] D,
  input  [1:0] Sel,
  output [3:0] O
);

  _1mux _1mux_1 (.Sel(Sel), .A(A[0]), .B(B[0]), .C(C[0]), .D(D[0]), .O(O[0]));
  _1mux _1mux_2 (.Sel(Sel), .A(A[1]), .B(B[1]), .C(C[1]), .D(D[1]), .O(O[1]));
  _1mux _1mux_3 (.Sel(Sel), .A(A[2]), .B(B[2]), .C(C[2]), .D(D[2]), .O(O[2]));
  _1mux _1mux_4 (.Sel(Sel), .A(A[3]), .B(B[3]), .C(C[3]), .D(D[3]), .O(O[3]));
endmodule
