// Digital circuit 4bitALU.dig as structural Verilog
module _4bitALU (
  input  [3:0] A,
  input  [3:0] B,
  input  OP,
  output [3:0] O,
  output Co
);

  wire [3:0] xor_1_out;

  xor xor_1 (xor_1_out[0], OP, B[0]);
  xor xor_2 (xor_1_out[1], OP, B[1]);
  xor xor_3 (xor_1_out[2], OP, B[2]);
  xor xor_4 (xor_1_out[3], OP, B[3]);
  _4bitAdderWC _4bitadderwc_1 (.A(A), .B(xor_1_out), .Ci(OP), .S(O), .Co(Co));
endmodule
