// Digital circuit 4bitAdder.dig as structural Verilog
module _4bitAdder (
  input  [3:0] A,
  input  [3:0] B,
  output [3:0] S,
  output C
);

  wire fulladder_1_co, fulladder_2_co, halfadder_1_c;

  halfAdder halfadder_1 (.A(A[0]), .B(B[0]), .S(S[0]), .C(halfadder_1_c));
  fullAdder fulladder_1 (.A(A[1]), .B(B[1]), .Ci(halfadder_1_c), .S(S[1]), .Co(fulladder_1_co));
  fullAdder fulladder_2 (.A(A[2]), .B(B[2]), .Ci(fulladder_1_co), .S(S[2]), .Co(fulladder_2_co));
  fullAdder fulladder_3 (.A(A[3]), .B(B[3]), .Ci(fulladder_2_co), .S(S[3]), .Co(C));
endmodule
