// Digital circuit 4bitAdderWC.dig as structural Verilog
module _4bitAdderWC (
  input  [3:0] A,
  input  [3:0] B,
  input  Ci,
  output [3:0] S,
  output Co
);

  wire fulladder_1_co, fulladder_2_co, fulladder_3_co;

  fullAdder fulladder_1 (.A(A[0]), .B(B[0]), .Ci(Ci), .S(S[0]), .Co(fulladder_1_co));
  fullAdder fulladder_2 (.A(A[1]), .B(B[1]), .Ci(fulladder_1_co), .S(S[1]), .Co(fulladder_2_co));
  fullAdder fulladder_3 (.A(A[2]), .B(B[2]), .Ci(fulladder_2_co), .S(S[2]), .Co(fulladder_3_co));
  fullAdder fulladder_4 (.A(A[3]), .B(B[3]), .Ci(fulladder_3_co), .S(S[3]), .Co(Co));
endmodule
