// Digital circuit 4bitBitShifter.dig as structural Verilog
module _4bitBitShifter (
  input  [3:0] I,
  input  lt__lt,
  output [3:0] O
);

  _1mux _1mux_1 (.A(I[1]), .B(1'b0), .Sel(lt__lt), .O(O[0]));
  _1mux _1mux_2 (.A(I[2]), .B(I[0]), .Sel(lt__lt), .O(O[1]));
  _1mux _1mux_3 (.A(I[3]), .B(I[1]), .Sel(lt__lt), .O(O[2]));
  _1mux _1mux_4 (.A(1'b0), .B(I[2]), .Sel(lt__lt), .O(O[3]));
endmodule
