// Digital circuit 4bitCPU.dig as structural Verilog
module _4bitCPU (
  input  [3:0] A,
  input  [3:0] B,
  input  CP,
  input  [1:0] OP,
  output [3:0] out_5,
  output out_6,
  output Done
);

  wire not_1_out, rslatch_1_q_2;
  wire [3:0] _1mux_1_o, _1mux_2_o, _1mux_3_o, _1mux_4_o, _1mux_5_o, _1mux_6_o, _1mux_7_o, _1mux_8_o,
       _4bitbitshifter_1_o, _4bitbitshifter_2_o, _4bitregister_1_q, _4bitregister_2_q, _4bitregister_3_q;

  rsLatch rslatch_1 (.R(CP), .S(Done), .Q_2(rslatch_1_q_2));  // open: Q
  _1mux _1mux_1 (.A(A), .B(_4bitbitshifter_1_o), .Sel(rslatch_1_q_2), .O(_1mux_1_o));
  _1mux _1mux_2 (.A(B), .B(_4bitbitshifter_2_o), .Sel(rslatch_1_q_2), .O(_1mux_2_o));
  // Probe on _1mux_1_o
  // Probe on _1mux_2_o
  _1mux _1mux_3 (.A(A), .B(_1mux_1_o), .Sel(OP[1]), .O(_1mux_3_o));
  _1mux _1mux_4 (.A(B), .B(_1mux_2_o), .Sel(OP[1]), .O(_1mux_4_o));
  _4bitRegister _4bitregister_1 (.D(_1mux_3_o), .CP(CP), .Q(_4bitregister_1_q));
  _4bitRegister _4bitregister_2 (.D(_1mux_4_o), .CP(CP), .Q(_4bitregister_2_q));
  _4bitBitShifter _4bitbitshifter_1 (.I(_4bitregister_1_q), .lt__lt(rslatch_1_q_2), .O(_4bitbitshifter_1_o));
  _4bitBitShifter _4bitbitshifter_2 (.I(_4bitregister_2_q), .lt__lt(not_1_out), .O(_4bitbitshifter_2_o));
  // Probe on _4bitregister_1_q
  // Probe on _4bitregister_2_q
  not not_1 (not_1_out, rslatch_1_q_2);
  _1mux _1mux_5 (.A(4'b0000), .B(_4bitregister_1_q), .Sel(_4bitregister_2_q[0]), .O(_1mux_5_o));
  _4bitEquals _4bitequals_1 (.A(_4bitregister_2_q), .B(4'b0000), .eq(Done));
  _1mux _1mux_6 (.A(_4bitregister_1_q), .B(_1mux_5_o), .Sel(OP[1]), .O(_1mux_6_o));
  _1mux _1mux_7 (.A(_4bitregister_2_q), .B(_4bitregister_3_q), .Sel(OP[1]), .O(_1mux_7_o));
  _4bitALU _1 (.A(_1mux_6_o), .B(_1mux_7_o), .OP(OP[0]), .O(out_5), .Co(out_6));
  _1mux _1mux_8 (.A(4'b0000), .B(out_5), .Sel(rslatch_1_q_2), .O(_1mux_8_o));
  _4bitRegister _4bitregister_3 (.D(_1mux_8_o), .CP(CP), .Q(_4bitregister_3_q));
  // Probe on _4bitregister_3_q
endmodule
