// Digital circuit 4bitEquals.dig as structural Verilog
module _4bitEquals (
  input  [3:0] A,
  input  [3:0] B,
  output eq
);

  wire nandand_1_c, nandand_2_c, nandnxor_1_y, nandnxor_2_y, nandnxor_3_y, nandnxor_4_y;

  nandNXOR nandnxor_1 (.A(A[0]), .B(B[0]), .Y(nandnxor_1_y));
  nandNXOR nandnxor_2 (.A(A[1]), .B(B[1]), .Y(nandnxor_2_y));
  nandNXOR nandnxor_3 (.A(A[2]), .B(B[2]), .Y(nandnxor_3_y));
  nandNXOR nandnxor_4 (.A(A[3]), .B(B[3]), .Y(nandnxor_4_y));
  nandAND nandand_1 (.A(nandnxor_1_y), .B(nandnxor_2_y), .C(nandand_1_c));
  nandAND nandand_2 (.A(nandnxor_3_y), .B(nandnxor_4_y), .C(nandand_2_c));
  nandAND nandand_3 (.A(nandand_1_c), .B(nandand_2_c), .C(eq));
endmodule
