// Digital circuit 4bitNegator.dig as structural Verilog
module _4bitNegator (
  input  [3:0] I,
  output [3:0] O
);

  wire [3:0] not_1_out;

  not not_1 (not_1_out[0], I[0]);
  not not_2 (not_1_out[1], I[1]);
  not not_3 (not_1_out[2], I[2]);
  not not_4 (not_1_out[3], I[3]);
  _4bitAdder _4bitadder_1 (.A(not_1_out), .B(4'b0001), .S(O));  // open: C
endmodule
