// Digital circuit 4bitRegister.dig as structural Verilog
module _4bitRegister (
  input  [3:0] D,
  input  CP,
  output [3:0] Q
);

  edgeLatch edgelatch_1 (.D(D[0]), .CP(CP), .Q(Q[0]));  // open: Q_2
  edgeLatch edgelatch_2 (.D(D[1]), .CP(CP), .Q(Q[1]));  // open: Q_2
  edgeLatch edgelatch_3 (.D(D[2]), .CP(CP), .Q(Q[2]));  // open: Q_2
  edgeLatch edgelatch_4 (.D(D[3]), .CP(CP), .Q(Q[3]));  // open: Q_2
endmodule
