// Digital circuit 4bitVersatileCounter.dig as structural Verilog
module _4bitVersatileCounter (
  input  CP,
  input  S,
  input  [3:0] D,
  input  [3:0] I,
  output [3:0] O
);

  wire [3:0] _1mux_1_o, _4bitadder_1_s;

  _1mux _1mux_1 (.A(_4bitadder_1_s), .B(D), .Sel(S), .O(_1mux_1_o));
  _4bitRegister _4bitregister_1 (.D(_1mux_1_o), .CP(CP), .Q(O));
  _4bitAdder _4bitadder_1 (.A(O), .B(I), .S(_4bitadder_1_s));  // open: C

  // Notes on the sheet:
  //   I: default 1
endmodule
