// Digital circuit badMultiplier.dig as structural Verilog
module badMultiplier (
  input  [3:0] A,
  input  [3:0] B,
  input  clk,
  output DONE,
  output [3:0] O
);

  wire rs_ff_as_1_q;
  wire [3:0] add_1_s, barrelshifter_1_out, barrelshifter_2_out, multiplexer_1_out, multiplexer_2_out,
       multiplexer_3_out, multiplexer_4_out, register_1_q, register_2_q;

  RS_FF_AS rs_ff_as_1 (.S(clk), .R(DONE), .Q(rs_ff_as_1_q));  // open: nQ
  Multiplexer #(.Bits(4)) multiplexer_1 (.sel(rs_ff_as_1_q), .in_0(4'b0000), .in_1(add_1_s), .out(multiplexer_1_out));
  Multiplexer #(.Bits(4)) multiplexer_2 (
    .sel(rs_ff_as_1_q), .in_0(B), .in_1(barrelshifter_2_out), .out(multiplexer_2_out));
  Multiplexer #(.Bits(4)) multiplexer_3 (
    .sel(rs_ff_as_1_q), .in_0(A), .in_1(barrelshifter_1_out), .out(multiplexer_3_out));
  BarrelShifter #(.Bits(4), .barrelSigned("true")) barrelshifter_1 (
    .in(register_1_q), .shift(4'b0001), .out(barrelshifter_1_out));
  BarrelShifter #(.Bits(4), .barrelSigned("true")) barrelshifter_2 (
    .in(register_2_q), .shift(4'b1111), .out(barrelshifter_2_out));
  Register #(.Bits(4)) register_1 (.D(multiplexer_3_out), .C(clk), .en(clk), .Q(register_1_q));
  Register #(.Bits(4)) register_2 (.D(multiplexer_2_out), .C(clk), .en(clk), .Q(register_2_q));
  Register #(.Bits(4)) register_3 (.D(multiplexer_1_out), .C(clk), .en(clk), .Q(O));
  Multiplexer #(.Bits(4)) multiplexer_4 (
    .sel(register_2_q[0]), .in_0(4'b0000), .in_1(register_1_q), .out(multiplexer_4_out));
  Comparator #(.Bits(4)) comparator_1 (.a(register_2_q), .b(4'b0000), .eq(DONE));  // open: gt, lt
  Add #(.Bits(4)) add_1 (.a(multiplexer_4_out), .b(O), .c_i(1'b0), .s(add_1_s));  // open: c_o
  LED led_1 (.in(DONE));
endmodule
