// Digital circuit cmosNAND.dig as structural Verilog
module cmosNAND (
  input  A,
  input  B,
  output O
);

  wire nfet_1_s;

  PFET pfet_1 (.G(A), .S(1'b1), .D(O));
  NFET nfet_1 (.G(A), .D(O), .S(nfet_1_s));
  NFET nfet_2 (.G(B), .D(nfet_1_s), .S(1'b0));
  PFET pfet_2 (.G(B), .S(1'b1), .D(O));
endmodule
