// Digital circuit cmosNOR.dig as structural Verilog
module cmosNOR (
  input  A,
  input  B,
  output O
);

  wire pfet_1_d;

  NFET nfet_1 (.G(A), .D(O), .S(1'b0));
  PFET pfet_1 (.G(A), .S(1'b1), .D(pfet_1_d));
  PFET pfet_2 (.G(B), .S(pfet_1_d), .D(O));
  NFET nfet_2 (.G(B), .D(O), .S(1'b0));
endmodule
