// Digital circuit dFlipFlop.dig as structural Verilog
module dFlipFlop (
  input  D,
  input  E,
  output Q,
  output Q_2
);

  wire nand_1_out, nand_2_out, not_1_out;

  not not_1 (not_1_out, D);
  nand nand_1 (nand_1_out, D, E);
  nand nand_2 (nand_2_out, E, not_1_out);
  rsLatch rslatch_1 (.R(nand_1_out), .S(nand_2_out), .Q(Q), .Q_2(Q_2));
endmodule
