// Digital circuit edgeLatch.dig as structural Verilog
module edgeLatch (
  input  D,
  input  CP,
  output Q,
  output Q_2
);

  wire dflipflop_1_q, not_1_out;

  not not_1 (not_1_out, CP);
  dFlipFlop dflipflop_1 (.D(D), .E(not_1_out), .Q(dflipflop_1_q));  // open: Q_2
  dFlipFlop dflipflop_2 (.D(dflipflop_1_q), .E(CP), .Q(Q), .Q_2(Q_2));
endmodule
