// Digital circuit halfAdder.dig as structural Verilog
module halfAdder (
  input  A,
  input  B,
  output S,
  output C
);

  wire nand_1_out, nand_2_out, nand_3_out;

  nand nand_1 (nand_1_out, A, B);
  nand nand_2 (nand_2_out, A, nand_1_out);
  nand nand_3 (nand_3_out, nand_1_out, B);
  not not_1 (C, nand_1_out);
  nand nand_4 (S, nand_2_out, nand_3_out);
endmodule
