// Digital circuit nandAND.dig as structural Verilog
module nandAND (
  input  A,
  input  B,
  output C
);

  wire nand_1_out;

  nand nand_1 (nand_1_out, A, B);
  not not_1 (C, nand_1_out);
endmodule
