// Digital circuit nandNXOR.dig as structural Verilog
module nandNXOR (
  input  A,
  input  B,
  output Y
);

  wire nand_1_out, nand_2_out, not_1_out, not_2_out;

  not not_1 (not_1_out, A);
  not not_2 (not_2_out, B);
  nand nand_1 (nand_1_out, not_1_out, not_2_out);
  nand nand_2 (nand_2_out, A, B);
  nand nand_3 (Y, nand_1_out, nand_2_out);
endmodule
