// Digital circuit rsFlipFlop.dig as structural Verilog
module rsFlipFlop (
  input  S,
  input  R,
  input  CP,
  output Q,
  output Q_2
);

  wire nand_1_out, nand_2_out;

  nand nand_1 (nand_1_out, S, CP);
  nand nand_2 (nand_2_out, CP, R);
  rsLatch rslatch_1 (.R(nand_1_out), .S(nand_2_out), .Q(Q), .Q_2(Q_2));
endmodule
